// Logisim project Decodercircuit.circ as structural Verilog: 1 circuit, main circuit main
module main (
);

  wire and_1_out, and_2_out, and_3_out, and_4_out, clock_1_out, clock_2_out, not_1_out, not_2_out;

  Clock clock_1 (.out(clock_1_out));
  Clock clock_2 (.out(clock_2_out));
  not not_1 (not_1_out, clock_1_out);
  not not_2 (not_2_out, clock_2_out);
  and and_1 (and_1_out, not_1_out, not_2_out);
  and and_2 (and_2_out, not_1_out, clock_2_out);
  and and_3 (and_3_out, clock_1_out, not_2_out);
  and and_4 (and_4_out, clock_1_out, clock_2_out);
  LED led_1 (.in(and_1_out));
  LED led_2 (.in(and_2_out));
  LED led_3 (.in(and_3_out));
  LED led_4 (.in(and_4_out));

  // Notes on the sheet:
  //   x
  //   y
  //   X'Y'
  //   X'Y
  //   XY'
  //   XY
endmodule
