// Logisim project MultiplexerCircuit.circ as structural Verilog: 1 circuit, main circuit main
module main (
);

  wire clock_1_out, clock_2_out, clock_3_out, clock_4_out, multiplexer_1_out, multiplexer_2_out, not_1_out,
       not_2_out, not_3_out;

  Clock clock_1 (.out(clock_1_out));
  Clock clock_2 (.out(clock_2_out));
  Clock clock_3 (.out(clock_3_out));
  Clock clock_4 (.out(clock_4_out));
  not not_1 (not_1_out, clock_1_out);
  Multiplexer multiplexer_1 (.in0(clock_1_out), .in1(not_1_out), .out(multiplexer_1_out), .sel(not_2_out));
  not not_2 (not_2_out, clock_3_out);
  not not_3 (not_3_out, clock_4_out);
  LED led_1 (.in(multiplexer_1_out));
  Multiplexer multiplexer_2 (.in0(clock_2_out), .in1(clock_2_out), .out(multiplexer_2_out), .sel(not_3_out));
  LED led_2 (.in(multiplexer_2_out));

  // Notes on the sheet:
  //   Multiplexer with NOT GATE that make both the signal to the output 
  //   Multiplexer with NOT GATE that make both the signal to the output 
endmodule
